// Logisim project DivideBy3.circ as structural Verilog: 1 circuit, main circuit main
module main (
  input  x,
  input  clock,
  input  reset,
  output Out
);

  wire and_1_out, and_2_out, and_3_out, and_4_out, and_5_out, d_ff_1_q, d_ff_1_qn, d_ff_2_q, d_ff_2_qn,
       not_1_out, not_2_out, not_3_out, not_4_out, not_5_out, or_1_out, or_2_out;

  not not_1 (not_1_out, reset);
  not not_2 (not_2_out, x);
  not not_3 (not_3_out, d_ff_1_q);
  not not_4 (not_4_out, d_ff_2_q);
  not not_5 (not_5_out, x);
  and and_1 (and_1_out, not_2_out, d_ff_2_q);
  and and_2 (and_2_out, d_ff_1_q, x);
  and and_3 (and_3_out, not_3_out, not_4_out);
  and and_4 (and_4_out, and_3_out, x);
  and and_5 (and_5_out, d_ff_1_q, not_5_out);
  or or_1 (or_1_out, and_1_out, and_2_out);
  or or_2 (or_2_out, and_4_out, and_5_out);
  D_Flip_Flop d_ff_1 (.clk(clock), .D(or_1_out), .Q(d_ff_1_q), .Qn(d_ff_1_qn), .reset(not_1_out));  // open: preset, en
  D_Flip_Flop d_ff_2 (.clk(clock), .D(or_2_out), .Q(d_ff_2_q), .Qn(d_ff_2_qn), .reset(not_1_out));  // open: preset, en
  and and_6 (Out, d_ff_1_qn, d_ff_2_qn);
endmodule
