// Logisim project SequenceDetector.circ as structural Verilog: 1 circuit, main circuit main
module main (
  input  In,
  input  Clk,
  input  reset,
  output Detect
);

  wire and_1_out, and_2_out, and_3_out, not_1_out, or_1_out, or_2_out, S0_q, S1_q;

  not not_1 (not_1_out, S0_q);
  and and_1 (and_1_out, S0_q, In);
  and and_2 (and_2_out, In, S1_q);
  or or_1 (or_1_out, Detect, and_1_out, and_2_out);
  and and_3 (and_3_out, not_1_out, In);
  or or_2 (or_2_out, Detect, and_2_out, and_3_out);
  D_Flip_Flop S1 (.clk(Clk), .D(or_1_out), .Q(S1_q), .reset(reset));  // open: Qn, preset, en
  D_Flip_Flop S0 (.clk(Clk), .D(or_2_out), .Q(S0_q), .reset(reset));  // open: Qn, preset, en
  and and_4 (Detect, S1_q, S0_q);
endmodule
