// Logisim project circuit1.circ as structural Verilog: 1 circuit, main circuit main
module main (
);

  wire not_1_out, pull_resistor_1_node, pull_resistor_2_node, undriven;

  LED led_1 ();  // open: in
  Pull_Resistor pull_resistor_1 (.node(pull_resistor_1_node));
  not not_1 (not_1_out, undriven);
  LED led_2 ();  // open: in
  Pull_Resistor pull_resistor_2 (.node(pull_resistor_2_node));
  // also tied to GND on the sheet: {pull_resistor_1_node, pull_resistor_2_node}

  // Notes on the sheet:
  //   330 Ohm
  //   Switch
  //   -
  //   +
  //   GND
  //   Inverter, 7404
  //   LED
  //   -
  //   LED
  //   +
  //   330 Ohm
  //   GND
endmodule
