// Logisim project decadeCounter.circ as structural Verilog: 1 circuit, main circuit main
module main (
  input  clock,
  input  reset
);

  wire A_2_q, and_1_out, and_2_out, and_3_out, and_4_out, and_5_out, and_6_out, and_7_out, B_2_q, C_2_q,
       D_2_q, not_1_out, not_2_out, not_3_out, not_4_out, not_5_out, not_6_out, not_7_out, not_8_out,
       or_1_out, or_2_out, or_3_out;

  // Probe on C_2_q
  // Probe on D_2_q
  // Probe on B_2_q
  not not_1 (not_1_out, A_2_q);
  not not_2 (not_2_out, C_2_q);
  not not_3 (not_3_out, B_2_q);
  not not_4 (not_4_out, A_2_q);
  // Probe on A_2_q
  and and_1 (and_1_out, A_2_q, B_2_q, C_2_q);
  and and_2 (and_2_out, not_1_out, D_2_q);
  and and_3 (and_3_out, A_2_q, B_2_q, not_2_out);
  and and_4 (and_4_out, not_3_out, C_2_q);
  and and_5 (and_5_out, not_4_out, C_2_q);
  D_Flip_Flop D_2 (.clk(clock), .D(or_1_out), .Q(D_2_q), .reset(reset));  // open: Qn, preset, en
  or or_1 (or_1_out, and_1_out, and_2_out);
  or or_2 (or_2_out, and_3_out, and_4_out, and_5_out);
  not not_5 (not_5_out, B_2_q);
  not not_6 (not_6_out, D_2_q);
  not not_7 (not_7_out, A_2_q);
  not not_8 (not_8_out, A_2_q);
  and and_6 (and_6_out, A_2_q, not_5_out, not_6_out);
  and and_7 (and_7_out, not_7_out, B_2_q);
  D_Flip_Flop C_2 (.clk(clock), .D(or_2_out), .Q(C_2_q), .reset(reset));  // open: Qn, preset, en
  or or_3 (or_3_out, and_6_out, and_7_out);
  D_Flip_Flop B_2 (.clk(clock), .D(or_3_out), .Q(B_2_q), .reset(reset));  // open: Qn, preset, en
  D_Flip_Flop A_2 (.clk(clock), .D(not_8_out), .Q(A_2_q), .reset(reset));  // open: Qn, preset, en
endmodule
