// Logisim project jan25.circ as structural Verilog: 1 circuit, main circuit main
module main (
  input  in_1,
  input  B
);

  wire nand_1_out, nand_2_out, nand_3_out;

  nand nand_1 (nand_1_out, in_1, 1'b1);
  nand nand_2 (nand_2_out, 1'b1, B);
  nand nand_3 (nand_3_out, nand_1_out, nand_2_out);
  LED led_1 (.in(nand_3_out));
endmodule
