// Logisim project tester.circ as structural Verilog: 1 circuit, main circuit main
module main (
  input  reset,
  output out_2,
  output [1:0] halt
);

  wire clock_out, comparator_1_eq;
  wire [5:0] ram_1_data;
  wire [7:0] counter_1_q;

  Clock clock (.out(clock_out));
  Counter counter_1 (.Q(counter_1_q), .clk(clock_out), .clr(reset));  // open: load, D, count, carry
  RAM ram_1 (.addr(counter_1_q), .data({halt, ram_1_data}), .ld(1'b1));  // open: sel, clk, clr
  Comparator #(.width(2)) comparator_1 (.a(ram_1_data[1:0]), .eq(comparator_1_eq));  // open: b, gt, lt
  LED led_1 (.in(out_2));
  not not_1 (out_2, comparator_1_eq);
endmodule
