// Logisim project tester2.circ as structural Verilog: 1 circuit, main circuit main
module main (
  input  reset,
  output [7:0] count,
  output [3:0] data,
  output [1:0] Outs,
  output Compare,
  output halt
);

  wire and_1_out, clock_1_out, not_1_out;

  Clock clock_1 (.out(clock_1_out));
  Counter counter_1 (.Q(count), .clk(clock_1_out), .clr(reset));  // open: load, D, count, carry
  not not_1 (not_1_out, reset);
  RAM #(.dataWidth(4)) ram_1 (.addr(count), .data(data), .ld(1'b1));  // open: sel, clk, clr
  DivideBy3_main main_1 (.x(data[1]), .clock(clock_1_out), .reset(and_1_out), .Out(Outs[0]));
  and and_1 (and_1_out, data[2], not_1_out);
  Comparator #(.width(1)) comparator_1 (.a(data[0]), .b(Outs[0]), .eq(Compare));  // open: gt, lt
  LED #(.active("false")) led_1 (.in(Compare));

  assign halt = data[3];
  assign Outs[1] = data[0];
endmodule
